# Fritzing sketch Robot_Structure (saved by Fritzing 0.9.10b)
breadboards: 1

parts:
  Part1 = Motor Driver 1A Dual TB6612FNG
  U1 = LIPO-1000mAh [package=lipo-1000]
  U2 = Voltage Regulator [package=v-reg_dpack]
  Part2 = Adafruit VL530X Time of Flight Distance Sensor [part_number="Adafruit #3317"]  # not connected
  Part3 = Adafruit VL530X Time of Flight Distance Sensor [part_number="Adafruit #3317"]  # not connected
  M3 = DC Motor [voltage_(max)=6V voltage_(min)=3V]
  M4 = DC Motor [voltage_(max)=6V voltage_(min)=3V]
  S1 = Taiway 100-SP-X-T1 SPDT Miniature Toggle Switch [part_number=100-SP-X-T1-0-0-B1-M2 package=THT]
  C1 = Electrolytic Capacitor [capacitance=10μF voltage=35V package="0605 [SMD, electrolytic]"]
  U3 = ESP32S-HiLetgo [part_number=ESP32S-HiLetgo]

nets:
  GND: Part1.GND, C1.-, U3.GND
  N1: Part1.B01, M4.pin_1
  N2: Part1.B02, M4.pin_2
  N3: Part1.A02, M3.pin_1
  N4: Part1.A01, M3.pin_2
  VCC: Part1.VCC, Part1.VM, S1.L2, C1.+, U3.VIN
  N5: U1.+, U2.IN
  N6: U2.OUT, S1.L1

custom parts:
  Adafruit VL530X Time of Flight Distance Sensor: The VL53L0X is a Time of Flight distance sensor like no other you've used! The sensor contains a very tiny invisible laser source, and a matching sensor. The VL53L0X can detect the "time of flight", or how long the light has taken to bounce back to the sensor. Since it uses a very narrow light source, it is good for determining distance of only the surface directly in front of it. Unlike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
  ESP32S-HiLetgo: HiLetgo ESP-WROOM-32 ESP32 ESP-32S Development Board 2.4GHz Dual-Mode WiFi + Bluetooth Dual Cores Microcontroller The ESP32 integrated with Antenna switches, RF Balun, power amplifiers, low-noise amplifiers, filters, and management modules, and the entire solution occupies the least area of PCB. 2.4 GHz Wi-Fi plus Bluetooth dual-mode chip, with TSMC Ultra-low power consumption 40nm technology,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
